# Fritzing sketch scanner (saved by Fritzing 0.9.3b)
circuit board: 13cm x 20cm
breadboards: 1

parts:
  BUZZER = Piezo Speaker
  Feather = Adafruit Feather HUZZAH ESP8266 [part_number="Adafruit #2821"]
  DISPLAY = SSD1305 I2C [package="SIP (Single Inline) [THT]"]
  S1 = Toggle Switch [package=THT]
  JP1 = Header 2 [package=jst-2-pth-kit]
  C1 = Electrolytic Capacitor [capacitance=100µF package="200 mil [THT, electrolytic]"]
  CHECKIN = Pushbutton [package="[THT]"]
  JMY622 = JMY622 [package=Other]

nets:
  GND: BUZZER.pin1, Feather.GND, DISPLAY.GND, DISPLAY.ADDR, JP1.1, C1.-, JMY622.GND, JMY622.CE
  N1: BUZZER.pin2, Feather.GPIO15
  N2: Feather.GPIO12/MISO, JMY622.TXD
  N3: Feather.GPIO13/MOSI, CHECKIN.Pin_3, CHECKIN.Pin_4
  N4: Feather.GPIO14/SCK, JMY622.RXD
  N5: Feather.3.3V, DISPLAY.3v, C1.+, CHECKIN.Pin_1, CHECKIN.Pin_2, JMY622.3V, JMY622.SPS
  N6: Feather.VBAT, S1.L1, JMY622.5V
  N7: Feather.GPIO2, DISPLAY.RST
  N8: Feather.GPIO5/SCL, DISPLAY.SCL
  N9: Feather.GPIO4/SDA, DISPLAY.SDA, DISPLAY.SDA2
  N10: S1.COM, JP1.2

custom parts:
  Adafruit Feather HUZZAH ESP8266: his is the Adafruit Feather HUZZAH ESP8266 - our take on an 'all-in-one' ESP8266 WiFi development board with built in USB and battery charging. Its an ESP8266 WiFi module with all the extras you need, ready to rock! We have other boards in the Feather family, check'em out here. At the Feather HUZZAH's heart is an ESP8266 WiFi microcontroller clocked at 80 MHz and at 3.3V logic. This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
  SSD1305 I2C: A SIP stand-in part for whatever you want. With 20 pins on a 300 mil single inline package (SIP) footprint.
