# Fritzing sketch scanner_squarepcb (saved by Fritzing 0.9.3b)
circuit board: 12cm x 9cm
breadboards: 1

parts:
  DISPLAY = SSD1305 I2C [package="SIP (Single Inline) [THT]"]
  S1 = Toggle Switch [package=THT]
  JP1 = Header 2 [package=jst-2-pth-kit]
  CHECKIN = Pushbutton [package="[THT]"]
  BUZZER = S1133 Si Photodiode [package="8mm Ceramic [THT]"]
  Feather = Adafruit Feather HUZZAH ESP8266 [part_number="Adafruit #2821"]
  100µF = Electrolytic Capacitor [capacitance=100µF package="200 mil [THT, electrolytic]"]
  JMY622 = JMY622 [package=Other]

nets:
  GND: DISPLAY.GND, DISPLAY.ADDR, DISPLAY.FRAME, JP1.1, CHECKIN.Pin_1, CHECKIN.Pin_2, BUZZER.anode, Feather.GND, 100µF.-, JMY622.GND, JMY622.CE
  N1: DISPLAY.3v, Feather.3.3V, 100µF.+, JMY622.3V, JMY622.SPS
  N2: DISPLAY.SCL, Feather.GPIO5/SCL
  N3: DISPLAY.SDA, DISPLAY.SDA2, Feather.GPIO4/SDA
  N4: DISPLAY.RST, Feather.GPIO2
  N5: S1.L1, Feather.VBAT, JMY622.5V
  N6: S1.COM, JP1.2
  N7: CHECKIN.Pin_3, CHECKIN.Pin_4, Feather.GPIO13/MOSI
  N8: BUZZER.cathode, Feather.GPIO15
  N9: Feather.GPIO12/MISO, JMY622.TXD
  N10: Feather.GPIO14/SCK, JMY622.RXD

custom parts:
  SSD1305 I2C: A SIP stand-in part for whatever you want. With 20 pins on a 300 mil single inline package (SIP) footprint.
  Adafruit Feather HUZZAH ESP8266: his is the Adafruit Feather HUZZAH ESP8266 - our take on an 'all-in-one' ESP8266 WiFi development board with built in USB and battery charging. Its an ESP8266 WiFi module with all the extras you need, ready to rock! We have other boards in the Feather family, check'em out here. At the Feather HUZZAH's heart is an ESP8266 WiFi microcontroller clocked at 80 MHz and at 3.3V logic. This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
