# Fritzing sketch v2.1 (saved by Fritzing 0.9.3b)
circuit board: 3.28358cm x 13cm
breadboards: 1

parts:
  ESP8266 = Adafruit Feather HUZZAH ESP8266 [part_number="Adafruit #2821"]
  U3 = SSD1305 I2C [package="SIP (Single Inline) [THT]"]
  100μF = Capacitor Polarized [package=cpol-radial-100uf-25v]
  S1 = Momentary Switch [package=tactile-pth]
  J1 = rounded female pin header, 5 pins [form="♀ (female rounded)"]  # not connected
  J2 = rounded female pin header, 1 pin [form="♀ (female rounded)"]  # not connected
  BUZZ = Buzzer 12mm [package=buzzer-12mm-ns]
  J3 = female pin header, 8 pins [form="♀ (female)"]
  OFF = Toggle Switch [package=THT]

nets:
  N1: ESP8266.GPIO12/MISO, J3.pin7
  N2: ESP8266.GPIO13/MOSI, S1.3
  N3: ESP8266.GPIO14/SCK, J3.pin6
  GND: ESP8266.GND, U3.GND, U3.ADDR, 100μF.-, S1.1, BUZZ.2, J3.pin3, J3.pin4, OFF.COM
  N4: ESP8266.3.3V, U3.3v, 100μF.+, J3.pin2, J3.pin5
  N5: ESP8266.VBAT, J3.pin1
  N6: ESP8266.EN, OFF.L1
  N7: ESP8266.GPIO15, BUZZ.1
  N8: ESP8266.GPIO2, U3.RST
  N9: ESP8266.GPIO5/SCL, U3.SCL
  N10: ESP8266.GPIO4/SDA, U3.SDA, U3.SDA2

notes:
  DISPLAY
  Deichman
  shelf scanner v2.1
  |||||||||||||
  +
  JMY622

custom parts:
  Adafruit Feather HUZZAH ESP8266: his is the Adafruit Feather HUZZAH ESP8266 - our take on an 'all-in-one' ESP8266 WiFi development board with built in USB and battery charging. Its an ESP8266 WiFi module with all the extras you need, ready to rock! We have other boards in the Feather family, check'em out here. At the Feather HUZZAH's heart is an ESP8266 WiFi microcontroller clocked at 80 MHz and at 3.3V logic. This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
  SSD1305 I2C: A SIP stand-in part for whatever you want. With 20 pins on a 300 mil single inline package (SIP) footprint.
