# Fritzing sketch v2 (saved by Fritzing 0.9.3b)
circuit board: 3.28358cm x 11.963cm
breadboards: 1

parts:
  ESP8266 = Adafruit Feather HUZZAH ESP8266 [part_number="Adafruit #2821"]
  U3 = SSD1305 I2C [package="SIP (Single Inline) [THT]"]
  100μF = Capacitor Polarized [package=cpol-radial-100uf-25v]
  S1 = Momentary Switch [package=tactile-pth]
  BUZZ = Buzzer 12mm [package=buzzer-12mm-ns]
  J2 = female pin header, 1 pin [form="♀ (female)"]  # not connected
  J1 = rounded female pin header, 5 pins [form="♀ (female rounded)"]  # not connected
  JMY622 = JMY622 [package=Other]

nets:
  N1: ESP8266.GPIO12/MISO, JMY622.TXD
  N2: ESP8266.GPIO13/MOSI, S1.1
  N3: ESP8266.GPIO14/SCK, JMY622.RXD
  GND: ESP8266.GND, U3.GND, U3.ADDR, 100μF.-, S1.2, S1.4, BUZZ.2, JMY622.GND, JMY622.CE
  N4: ESP8266.3.3V, U3.3v, 100μF.+, JMY622.3V, JMY622.SPS
  N5: ESP8266.VBAT, JMY622.5V
  N6: ESP8266.GPIO15, BUZZ.1
  N7: ESP8266.GPIO2, U3.RST
  N8: ESP8266.GPIO5/SCL, U3.SCL
  N9: ESP8266.GPIO4/SDA, U3.SDA, U3.SDA2

notes:
  DISPLAY
  Deichman
  shelf scanner v0.2

custom parts:
  Adafruit Feather HUZZAH ESP8266: his is the Adafruit Feather HUZZAH ESP8266 - our take on an 'all-in-one' ESP8266 WiFi development board with built in USB and battery charging. Its an ESP8266 WiFi module with all the extras you need, ready to rock! We have other boards in the Feather family, check'em out here. At the Feather HUZZAH's heart is an ESP8266 WiFi microcontroller clocked at 80 MHz and at 3.3V logic. This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
  SSD1305 I2C: A SIP stand-in part for whatever you want. With 20 pins on a 300 mil single inline package (SIP) footprint.
